# Fritzing sketch 20190227_PCB_SAC (saved by Fritzing 0.9.3b)
circuit board: 8.53cm x 9cm
breadboards: 1

parts:
  J1 = Camdenboss CTB0158-4 [part_number=CTB0158-4 package=THT]
  J4 = Camdenboss CTB0158-4 [part_number=CTB0158-4 package=THT]
  M1 = SO08-EIAJ [chip_label=SO08-EIAJ package=SO]
  M2 = SO08-EIAJ [chip_label=SO08-EIAJ package=SO]
  M3 = SO08-EIAJ [chip_label=SO08-EIAJ package=SO]
  J3 = double row male pin header, 40 pins [form="♂ (male)"]
  R2 = Resistor [tolerance=±5% resistance=10k package="1206 [SMD]"]
  R1 = Resistor [tolerance=±5% resistance=10k package="1206 [SMD]"]
  R3 = Resistor [tolerance=±5% resistance=10k package="1206 [SMD]"]
  R4 = Resistor [tolerance=±5% resistance=1M package="1206 [SMD]"]
  R6 = Resistor [tolerance=±5% resistance=1M package="1206 [SMD]"]
  R5 = Resistor [tolerance=±5% resistance=1M package="1206 [SMD]"]
  J5 = Dagu DGServo 9g header (male) [package=THT]
  J6 = Dagu DGServo 9g header (male) [package=THT]
  R7 = Resistor [tolerance=±5% resistance=10k package="1206 [SMD]"]
  M4 = SO08-EIAJ [chip_label=SO08-EIAJ package=SO]
  R8 = Resistor [tolerance=±5% resistance=1M package="1206 [SMD]"]

nets:
  N1: J1.pin1, J4.pin1, M1.1, M1.2, M1.3, J3.pin38, R4.Pin_1, J5.gnd, J5.pulse, M4.1, M4.2, M4.3, R8.Pin_1
  N2: J1.pin2, M3.5, M3.6, M3.7, M3.8
  N3: J1.pin3, M2.5, M2.6, M2.7, M2.8
  N4: J1.pin4, M1.5, M1.6, M1.7, M1.8
  N5: J4.pin2, J3.pin40, J5.Vcc
  N6: J4.pin3, M4.5, M4.6, M4.7, M4.8
  N7: J4.pin4, J6.gnd
  N8: M1.4, R1.Pin_0, R4.Pin_0
  N9: M2.1, M2.2, M2.3, R5.Pin_1
  N10: M2.4, R2.Pin_0, R5.Pin_0
  N11: M3.1, M3.2, M3.3, R6.Pin_1
  N12: M3.4, R3.Pin_0, R6.Pin_0
  N13: J3.pin6, R1.Pin_1
  N14: J3.pin7, R2.Pin_1
  N15: J3.pin8, R3.Pin_1
  N16: J3.pin33, R7.Pin_1
  N17: R7.Pin_0, M4.4, R8.Pin_0

notes:
  GND
  5V
  -RLY
  +RLY
  1  2  3 COM
